// Logisim project processor.circ as structural Verilog: 7 circuits, main circuit Processor-Pipeline
module main (
  input  in_1
);

  wire Clock, En0, En1, En2, En3, En4, En5, En6, En7, En8, En9, En10, En11, En12, En13, En14, En15, En16,
       En17, En18, En19, En20, En21, En22, En23, En24, En25, En26, En27, En28, En29, En30, En31,
       En___Select____Reg___RB, En___Select___RA, En___Select___RC;
  wire [4:0] Select___RA, Select___RC, Select__Reg___RB;
  wire [31:0] Input, MUX_B, O0, O1, O2, O3, O4, O5, O6, O7, O8, O9, O10, O11, O12, O13, O14, O15, O16, O17,
       O18, O19, O20, O21, O22, O23, O24, O25, O26, O27, O28, O29, O30, O31, RA;

  Clock clock_1 (.out(Clock));
  // Probe on O0
  // Probe on O8
  // Probe on O16
  // Probe on O24
  Register #(.width(32)) R0 (.D(Input), .en(En0), .Q(O0), .clk(Clock), .clr(in_1));
  Register #(.width(32)) R8 (.D(Input), .en(En8), .Q(O8), .clk(Clock), .clr(in_1));
  Register #(.width(32)) R16 (.D(Input), .en(En16), .Q(O16), .clk(Clock), .clr(in_1));
  Register #(.width(32)) R24 (.D(Input), .en(En24), .Q(O24), .clk(Clock), .clr(in_1));
  Register #(.width(32)) R1 (.D(Input), .en(En1), .Q(O1), .clk(Clock), .clr(in_1));
  Register #(.width(32)) R9 (.D(Input), .en(En9), .Q(O9), .clk(Clock), .clr(in_1));
  Register #(.width(32)) R17 (.D(Input), .en(En17), .Q(O17), .clk(Clock), .clr(in_1));
  Register #(.width(32)) R25 (.D(Input), .en(En25), .Q(O25), .clk(Clock), .clr(in_1));
  // Probe on Select___RC
  // Probe on O1
  // Probe on O9
  // Probe on O17
  // Probe on O25
  Demultiplexer #(.select(5)) demultiplexer_1 (
    .out0(En0), .out1(En1), .out2(En2), .out3(En3), .out4(En4), .out5(En5), .out6(En6), .out7(En7),
    .out8(En8), .out9(En9), .out10(En10), .out11(En11), .out12(En12), .out13(En13), .out14(En14),
    .out15(En15), .out16(En16), .out17(En17), .out18(En18), .out19(En19), .out20(En20), .out21(En21),
    .out22(En22), .out23(En23), .out24(En24), .out25(En25), .out26(En26), .out27(En27), .out28(En28),
    .out29(En29), .out30(En30), .out31(En31), .in(1'b1), .sel(Select___RC), .en(En___Select___RC));
  // Probe on O2
  // Probe on O10
  // Probe on O18
  // Probe on O26
  Register #(.width(32)) R2 (.D(Input), .en(En2), .Q(O2), .clk(Clock), .clr(in_1));
  Register #(.width(32)) R10 (.D(Input), .en(En10), .Q(O10), .clk(Clock), .clr(in_1));
  Register #(.width(32)) R18 (.D(Input), .en(En18), .Q(O18), .clk(Clock), .clr(in_1));
  Register #(.width(32)) R26 (.D(Input), .en(En26), .Q(O26), .clk(Clock), .clr(in_1));
  // Probe on Select___RA
  Register #(.width(32)) R3 (.D(Input), .en(En3), .Q(O3), .clk(Clock), .clr(in_1));
  Register #(.width(32)) R11 (.D(Input), .en(En11), .Q(O11), .clk(Clock), .clr(in_1));
  Register #(.width(32)) R19 (.D(Input), .en(En19), .Q(O19), .clk(Clock), .clr(in_1));
  Register #(.width(32)) R27 (.D(Input), .en(En27), .Q(O27), .clk(Clock), .clr(in_1));
  // Probe on Select__Reg___RB
  // Probe on O3
  // Probe on O11
  // Probe on O19
  // Probe on O27
  // Probe on O4
  // Probe on O12
  // Probe on O20
  // Probe on O28
  Register #(.width(32)) R4 (.D(Input), .en(En4), .Q(O4), .clk(Clock), .clr(in_1));
  Register #(.width(32)) R12 (.D(Input), .en(En12), .Q(O12), .clk(Clock), .clr(in_1));
  Register #(.width(32)) R20 (.D(Input), .en(En20), .Q(O20), .clk(Clock), .clr(in_1));
  Register #(.width(32)) R28 (.D(Input), .en(En28), .Q(O28), .clk(Clock), .clr(in_1));
  // Probe on RA
  Multiplexer #(.select(5), .width(32)) multiplexer_1 (
    .in0(O0), .in1(O1), .in2(O2), .in3(O3), .in4(O4), .in5(O5), .in6(O6), .in7(O7), .in8(O8), .in9(O9),
    .in10(O10), .in11(O11), .in12(O12), .in13(O13), .in14(O14), .in15(O15), .in16(O16), .in17(O17),
    .in18(O18), .in19(O19), .in20(O20), .in21(O21), .in22(O22), .in23(O23), .in24(O24), .in25(O25),
    .in26(O26), .in27(O27), .in28(O28), .in29(O29), .in30(O30), .in31(O31), .out(RA), .sel(Select___RA),
    .en(En___Select___RA));
  Register #(.width(32)) R5 (.D(Input), .en(En5), .Q(O5), .clk(Clock), .clr(in_1));
  Register #(.width(32)) R13 (.D(Input), .en(En13), .Q(O13), .clk(Clock), .clr(in_1));
  Register #(.width(32)) R21 (.D(Input), .en(En21), .Q(O21), .clk(Clock), .clr(in_1));
  Register #(.width(32)) R29 (.D(Input), .en(En29), .Q(O29), .clk(Clock), .clr(in_1));
  // Probe on MUX_B
  // Probe on O5
  // Probe on O13
  // Probe on O21
  // Probe on O29
  // Probe on O6
  // Probe on O14
  // Probe on O22
  // Probe on O30
  Register #(.width(32)) R6 (.D(Input), .en(En6), .Q(O6), .clk(Clock), .clr(in_1));
  Register #(.width(32)) R14 (.D(Input), .en(En14), .Q(O14), .clk(Clock), .clr(in_1));
  Register #(.width(32)) R22 (.D(Input), .en(En22), .Q(O22), .clk(Clock), .clr(in_1));
  Register #(.width(32)) R30 (.D(Input), .en(En30), .Q(O30), .clk(Clock), .clr(in_1));
  Multiplexer #(.select(5), .width(32)) multiplexer_2 (
    .in0(O0), .in1(O1), .in2(O2), .in3(O3), .in4(O4), .in5(O5), .in6(O6), .in7(O7), .in8(O8), .in9(O9),
    .in10(O10), .in11(O11), .in12(O12), .in13(O13), .in14(O14), .in15(O15), .in16(O16), .in17(O17),
    .in18(O18), .in19(O19), .in20(O20), .in21(O21), .in22(O22), .in23(O23), .in24(O24), .in25(O25),
    .in26(O26), .in27(O27), .in28(O28), .in29(O29), .in30(O30), .in31(O31), .out(MUX_B),
    .sel(Select__Reg___RB), .en(En___Select____Reg___RB));
  Register #(.width(32)) R7 (.D(Input), .en(En7), .Q(O7), .clk(Clock), .clr(in_1));
  Register #(.width(32)) R15 (.D(Input), .en(En15), .Q(O15), .clk(Clock), .clr(in_1));
  Register #(.width(32)) R23 (.D(Input), .en(En23), .Q(O23), .clk(Clock), .clr(in_1));
  Register #(.width(32)) R31 (.D(Input), .en(En31), .Q(O31), .clk(Clock), .clr(in_1));
  // Probe on O7
  // Probe on O15
  // Probe on O23
  // Probe on O31

  // Other names for the same wires on the sheet: Clear = in_1
endmodule

module Register_File (
  input  Clock,
  input  [4:0] Select_RC,
  input  [4:0] Select_RA,
  input  [4:0] Select_RB,
  input  [31:0] Input_RC,
  input  Clear_RF,
  input  En_Select_RC,
  input  En_Select_RA,
  input  En_Select_RB,
  output [31:0] RA,
  output [31:0] RB
);

  wire En0, En1, En2, En3, En4, En5, En6, En7, En8, En9, En10, En11, En12, En13, En14, En15, En16, En17,
       En18, En19, En20, En21, En22, En23, En24, En25, En26, En27, En28, En29, En30, En31;
  wire [31:0] O0, O1, O2, O3, O4, O5, O6, O7, O8, O9, O10, O11, O12, O13, O14, O15, O16, O17, O18, O19, O20,
       O21, O22, O23, O24, O25, O26, O27, O28, O29, O30, O31;

  // Probe on O0
  // Probe on O8
  // Probe on O16
  // Probe on O24
  Register #(.width(32)) R0 (.D(Input_RC), .en(En0), .Q(O0), .clk(Clock), .clr(Clear_RF));
  Register #(.width(32)) R8 (.D(Input_RC), .en(En8), .Q(O8), .clk(Clock), .clr(Clear_RF));
  Register #(.width(32)) R16 (.D(Input_RC), .en(En16), .Q(O16), .clk(Clock), .clr(Clear_RF));
  Register #(.width(32)) R24 (.D(Input_RC), .en(En24), .Q(O24), .clk(Clock), .clr(Clear_RF));
  Register #(.width(32)) R1 (.D(Input_RC), .en(En1), .Q(O1), .clk(Clock), .clr(Clear_RF));
  Register #(.width(32)) R9 (.D(Input_RC), .en(En9), .Q(O9), .clk(Clock), .clr(Clear_RF));
  Register #(.width(32)) R17 (.D(Input_RC), .en(En17), .Q(O17), .clk(Clock), .clr(Clear_RF));
  Register #(.width(32)) R25 (.D(Input_RC), .en(En25), .Q(O25), .clk(Clock), .clr(Clear_RF));
  // Probe on O1
  // Probe on O9
  // Probe on O17
  // Probe on O25
  Demultiplexer #(.select(5), .disabled(0)) demultiplexer_1 (
    .out0(En0), .out1(En1), .out2(En2), .out3(En3), .out4(En4), .out5(En5), .out6(En6), .out7(En7),
    .out8(En8), .out9(En9), .out10(En10), .out11(En11), .out12(En12), .out13(En13), .out14(En14),
    .out15(En15), .out16(En16), .out17(En17), .out18(En18), .out19(En19), .out20(En20), .out21(En21),
    .out22(En22), .out23(En23), .out24(En24), .out25(En25), .out26(En26), .out27(En27), .out28(En28),
    .out29(En29), .out30(En30), .out31(En31), .in(1'b1), .sel(Select_RC), .en(En_Select_RC));
  // Probe on O2
  // Probe on O10
  // Probe on O18
  // Probe on O26
  Register #(.width(32)) R2 (.D(Input_RC), .en(En2), .Q(O2), .clk(Clock), .clr(Clear_RF));
  Register #(.width(32)) R10 (.D(Input_RC), .en(En10), .Q(O10), .clk(Clock), .clr(Clear_RF));
  Register #(.width(32)) R18 (.D(Input_RC), .en(En18), .Q(O18), .clk(Clock), .clr(Clear_RF));
  Register #(.width(32)) R26 (.D(Input_RC), .en(En26), .Q(O26), .clk(Clock), .clr(Clear_RF));
  Register #(.width(32)) R3 (.D(Input_RC), .en(En3), .Q(O3), .clk(Clock), .clr(Clear_RF));
  Register #(.width(32)) R11 (.D(Input_RC), .en(En11), .Q(O11), .clk(Clock), .clr(Clear_RF));
  Register #(.width(32)) R19 (.D(Input_RC), .en(En19), .Q(O19), .clk(Clock), .clr(Clear_RF));
  Register #(.width(32)) R27 (.D(Input_RC), .en(En27), .Q(O27), .clk(Clock), .clr(Clear_RF));
  // Probe on O3
  // Probe on O11
  // Probe on O19
  // Probe on O27
  // Probe on Select_RA
  // Probe on O4
  // Probe on O12
  // Probe on O20
  // Probe on O28
  Register #(.width(32)) R4 (.D(Input_RC), .en(En4), .Q(O4), .clk(Clock), .clr(Clear_RF));
  Register #(.width(32)) R12 (.D(Input_RC), .en(En12), .Q(O12), .clk(Clock), .clr(Clear_RF));
  Register #(.width(32)) R20 (.D(Input_RC), .en(En20), .Q(O20), .clk(Clock), .clr(Clear_RF));
  Register #(.width(32)) R28 (.D(Input_RC), .en(En28), .Q(O28), .clk(Clock), .clr(Clear_RF));
  // Probe on RA
  Multiplexer #(.select(5), .width(32), .disabled(0)) multiplexer_1 (
    .in0(O0), .in1(O1), .in2(O2), .in3(O3), .in4(O4), .in5(O5), .in6(O6), .in7(O7), .in8(O8), .in9(O9),
    .in10(O10), .in11(O11), .in12(O12), .in13(O13), .in14(O14), .in15(O15), .in16(O16), .in17(O17),
    .in18(O18), .in19(O19), .in20(O20), .in21(O21), .in22(O22), .in23(O23), .in24(O24), .in25(O25),
    .in26(O26), .in27(O27), .in28(O28), .in29(O29), .in30(O30), .in31(O31), .out(RA), .sel(Select_RA),
    .en(En_Select_RA));
  Register #(.width(32)) R5 (.D(Input_RC), .en(En5), .Q(O5), .clk(Clock), .clr(Clear_RF));
  Register #(.width(32)) R13 (.D(Input_RC), .en(En13), .Q(O13), .clk(Clock), .clr(Clear_RF));
  Register #(.width(32)) R21 (.D(Input_RC), .en(En21), .Q(O21), .clk(Clock), .clr(Clear_RF));
  Register #(.width(32)) R29 (.D(Input_RC), .en(En29), .Q(O29), .clk(Clock), .clr(Clear_RF));
  // Probe on O5
  // Probe on O13
  // Probe on O21
  // Probe on O29
  // Probe on O6
  // Probe on O14
  // Probe on O22
  // Probe on O30
  // Probe on Select_RB
  Register #(.width(32)) R6 (.D(Input_RC), .en(En6), .Q(O6), .clk(Clock), .clr(Clear_RF));
  Register #(.width(32)) R14 (.D(Input_RC), .en(En14), .Q(O14), .clk(Clock), .clr(Clear_RF));
  Register #(.width(32)) R22 (.D(Input_RC), .en(En22), .Q(O22), .clk(Clock), .clr(Clear_RF));
  Register #(.width(32)) R30 (.D(Input_RC), .en(En30), .Q(O30), .clk(Clock), .clr(Clear_RF));
  Multiplexer #(.select(5), .width(32), .disabled(0)) multiplexer_2 (
    .in0(O0), .in1(O1), .in2(O2), .in3(O3), .in4(O4), .in5(O5), .in6(O6), .in7(O7), .in8(O8), .in9(O9),
    .in10(O10), .in11(O11), .in12(O12), .in13(O13), .in14(O14), .in15(O15), .in16(O16), .in17(O17),
    .in18(O18), .in19(O19), .in20(O20), .in21(O21), .in22(O22), .in23(O23), .in24(O24), .in25(O25),
    .in26(O26), .in27(O27), .in28(O28), .in29(O29), .in30(O30), .in31(O31), .out(RB), .sel(Select_RB),
    .en(En_Select_RB));
  Register #(.width(32)) R7 (.D(Input_RC), .en(En7), .Q(O7), .clk(Clock), .clr(Clear_RF));
  Register #(.width(32)) R15 (.D(Input_RC), .en(En15), .Q(O15), .clk(Clock), .clr(Clear_RF));
  Register #(.width(32)) R23 (.D(Input_RC), .en(En23), .Q(O23), .clk(Clock), .clr(Clear_RF));
  Register #(.width(32)) R31 (.D(Input_RC), .en(En31), .Q(O31), .clk(Clock), .clr(Clear_RF));
  // Probe on O7
  // Probe on O15
  // Probe on O23
  // Probe on O31
  // Probe on RB

  // Other names for the same wires on the sheet: Clear = Clear_RF; Input[31:0] = Input_RC
endmodule

module Processor (
);

  wire Clear_RZ, Clock, En_MUX_Y, En_RY, En_RZ, Select_MUX_Y, undriven;
  wire [31:0] alu_1_out_rz, Immediate, multiplexer_1_out, register_file_1_ra, register_file_1_rb, RY, RZ_q,
       undriven_2, undriven_3, undriven_4;

  // Probe on undriven
  Register_File register_file_1 (
    .RA(register_file_1_ra), .RB(register_file_1_rb), .Clock(Clock));  // open: Clear_RF, En_Select_RC, En_Select_RA, En_Select_RB, Select_RC, Select_RA, Select_RB, Input_RC
  RA_RB_Immediate ra_rb_immediate_1 (
    .Clock(Clock), .Immediate(Immediate), .Out_RA(undriven_2), .Out_MUX_RB(undriven_3),
    .In_RA(register_file_1_ra), .In_RB(register_file_1_rb));  // open: En_RA, En_RB, Clear_RA, Clear_RB, Select_MUX_B, En_MUX_B
  ALU alu_1 (.In_RA(undriven_2), .In_MUX_B(undriven_3), .Out_RZ(alu_1_out_rz));  // open: Select_ALU, Enable_ALU
  Register #(.width(32)) RZ (.D(alu_1_out_rz), .en(En_RZ), .Q(RZ_q), .clk(Clock), .clr(Clear_RZ));
  Multiplexer #(.width(32)) multiplexer_1 (
    .in0(RZ_q), .in1(undriven_4), .out(multiplexer_1_out), .sel(Select_MUX_Y), .en(En_MUX_Y));
  Register #(.width(32)) u_RY (.D(multiplexer_1_out), .en(En_RY), .Q(RY), .clk(Clock), .clr(Clear_RZ));
endmodule

module ALU (
  input  [31:0] In_RA,
  input  [31:0] In_MUX_B,
  input  [1:0] Select_ALU,
  input  Enable_ALU,
  output [31:0] Out_RZ
);

  wire [31:0] tunnel, tunnel_t, tunnel_t_t, x;

  Adder #(.width(32)) adder_1 (.a(In_RA), .b(In_MUX_B), .out(tunnel), .cin(1'b0));  // open: cout
  Subtractor #(.width(32)) subtractor_1 (.a(In_RA), .b(In_MUX_B), .out(tunnel_t), .bin(1'b0));  // open: bout
  Multiplier #(.width(32)) multiplier_1 (.a(In_RA), .b(In_MUX_B), .out(x), .cin({32{1'b0}}));  // open: cout
  Divider #(.width(32)) divider_1 (.a(In_RA), .b(In_MUX_B), .out(tunnel_t_t), .upper({32{1'b0}}));  // open: rem
  Multiplexer #(.select(2), .width(32)) multiplexer_1 (
    .in0(tunnel), .in1(tunnel_t), .in2(x), .in3(tunnel_t_t), .out(Out_RZ), .sel(Select_ALU), .en(Enable_ALU));

  // Other names for the same wires on the sheet: Output[31:0] = Out_RZ; RA[31:0] = In_RA; RB[31:0] = In_MUX_B
endmodule

module RA_RB_Immediate (
  input  [31:0] In_RA,
  input  [31:0] In_RB,
  input  [31:0] Out_RA,
  input  Clock,
  input  En_RA,
  input  En_RB,
  input  Clear_RA,
  input  Clear_RB,
  input  Select_MUX_B,
  input  En_MUX_B,
  input  [31:0] Immediate,
  input  [31:0] Out_MUX_RB
);

  wire [31:0] Out_RB;

  Register #(.width(32)) RA (.D(In_RA), .en(En_RA), .Q(Out_RA), .clk(Clock), .clr(Clear_RA));
  Multiplexer #(.width(32)) multiplexer_1 (
    .in0(Out_RB), .in1(Immediate), .out(Out_MUX_RB), .sel(Select_MUX_B), .en(En_MUX_B));
  Register #(.width(32)) RB (.D(In_RB), .en(En_RB), .Q(Out_RB), .clk(Clock), .clr(Clear_RB));
endmodule

module Processor_Pipeline (
  input  in_1,
  input  in_2
);

  wire Clear___RF, Clear_IR, Clear_PC, Clear_RA, Clear_Ram, Clear_RB, Clear_RM, Clear_RY, Clear_RZ, Clock,
       CS, En_ALU, En_IR, En_MUX_B, En_MUX_Y, En_PC, En_RA, En_RB, En_RM, En_RY, En_RZ, En_Select_RA,
       En_Select_RB, En_Select_RC, Enable_MUX_MA, Enable_PCSet, Enable_to_MUX_Y, Jump_Signal, Load_Signal,
       Load_Write_Ram, Move_Signal, not_1_out, Select_MUX_B, Select_MUX_MA, Select_MUX_Y, Select_PCSet,
       Signal, Signal_t, Store_Signal, Subtract_Signal, x_Signal;
  wire [1:0] Select_ALU;
  wire [2:0] Op_Code;
  wire [4:0] Select_RA, Select_RB;
  wire [17:0] Address;
  wire [18:0] Immediate;
  wire [31:0] adder_1_out, alu_1_out_rz, In_MUX_Y, Input_IR, multiplexer_1_out, multiplexer_2_out,
       multiplexer_3_out, Out_RAM, Out_RZ, PC_q, RA_q, RB_q, register_file_1_ra, register_file_1_rb, RY;
  wire [31:19] MemoryAddress;

  Clock clock_1 (.out(Clock));
  Register #(.width(32)) RA (.D(register_file_1_ra), .en(En_RA), .Q(RA_q), .clk(Clock), .clr(Clear_RA));
  // Probe on Select_ALU
  Register_File register_file_1 (
    .Clear_RF(Clear___RF), .En_Select_RC(En_Select_RC), .En_Select_RA(En_Select_RA),
    .En_Select_RB(En_Select_RB), .Select_RC(Select_RB), .Select_RA(Select_RA), .Select_RB(Select_RB),
    .RA(register_file_1_ra), .RB(register_file_1_rb), .Clock(Clock), .Input_RC(RY));
  Register #(.width(32)) RB (.D(register_file_1_rb), .en(En_RB), .Q(RB_q), .clk(Clock), .clr(Clear_RB));
  ALU alu_1 (
    .In_RA(RA_q), .In_MUX_B(multiplexer_1_out), .Out_RZ(alu_1_out_rz), .Select_ALU(Select_ALU),
    .Enable_ALU(En_ALU));
  Register #(.width(32)) RZ (.D(alu_1_out_rz), .en(En_RZ), .Q(Out_RZ), .clk(Clock), .clr(Clear_RZ));
  Multiplexer #(.width(32)) multiplexer_1 (
    .in0(RB_q), .in1({{13{in_1}}, Immediate}), .out(multiplexer_1_out), .sel(Select_MUX_B), .en(En_MUX_B));
  Multiplexer #(.width(32)) multiplexer_2 (
    .in0(Out_RZ), .in1(In_MUX_Y), .out(multiplexer_2_out), .sel(Select_MUX_Y), .en(En_MUX_Y));
  Register #(.width(32)) u_RY (.D(multiplexer_2_out), .en(En_RY), .Q(RY), .clk(Clock), .clr(Clear_RY));
  Register #(.width(32)) RM (.D(RB_q), .en(En_RM), .Q(Out_RAM), .clk(Clock), .clr(Clear_RM));
  // Probe on Out_RZ
  // Probe on In_MUX_Y
  // Probe on Out_RAM
  // Probe on CS
  Register #(.width(32)) IR (
    .D(Input_IR), .en(En_IR), .Q({Op_Code, Select_RA, Select_RB, Immediate}), .clk(Clock), .clr(Clear_IR));
  Multiplexer #(.width(32)) multiplexer_3 (
    .in0({{13{in_1}}, Immediate}), .in1(adder_1_out), .out(multiplexer_3_out), .sel(Select_PCSet),
    .en(Enable_PCSet));
  // Probe on {MemoryAddress, CS, Address}
  Multiplexer #(.width(32)) multiplexer_4 (
    .in0(Input_IR), .in1(Out_RAM), .out(In_MUX_Y), .sel(CS), .en(Enable_to_MUX_Y));
  // Probe on {Op_Code, Select_RA, Select_RB, Immediate}
  Register #(.width(32)) PC (.D(multiplexer_3_out), .en(En_PC), .Q(PC_q), .clk(Clock), .clr(Clear_PC));
  // Probe on Address
  not not_1 (not_1_out, CS);
  Multiplexer #(.width(32)) multiplexer_5 (
    .in0(Out_RZ), .in1(PC_q), .out({MemoryAddress, CS, Address}), .sel(Select_MUX_MA), .en(Enable_MUX_MA));
  Adder #(.width(32)) adder_1 (.a(PC_q), .b(32'h1), .out(adder_1_out), .cin(in_2));  // open: cout
  // Probe on Input_IR
  ROM #(.addrWidth(18), .dataWidth(32)) rom_1 (.addr(Address), .data(Input_IR), .sel(not_1_out));
  // Probe on Out_RAM
  RAM #(.addrWidth(18), .dataWidth(32)) ram_1 (
    .addr(Address), .data(Out_RAM), .sel(CS), .clk(Clock), .ld(Load_Write_Ram), .clr(Clear_Ram));
  Decoder #(.select(3), .enable("false")) decoder_1 (
    .out0(Load_Signal), .out1(Store_Signal), .out2(Move_Signal), .out3(Jump_Signal), .out4(Signal),
    .out5(Subtract_Signal), .out6(x_Signal), .out7(Signal_t), .sel(Op_Code));
  Control_Unit control_unit_1 (
    .Load_Signal(Load_Signal), .Store_Signal(Store_Signal), .Move_Signal(Move_Signal),
    .Jump_Signal(Jump_Signal), .Signal(Signal), .Subtract_Signal(Subtract_Signal), .x_Signal(x_Signal),
    .Signal_2(Signal_t), .Clock(Clock), .En_IR(En_IR), .En_PC(En_PC), .Select_MUX_MA(Select_MUX_MA),
    .Enable_MUX_MA(Enable_MUX_MA), .Enable_PCSet(Enable_PCSet), .Select_PCSet(Select_PCSet), .En_RA(En_RA),
    .En_RB(En_RB), .En_Select_RA(En_Select_RA), .En_Select_RB(En_Select_RB), .En_RZ(En_RZ),
    .Select_ALU(Select_ALU), .En_RM(En_RM), .En_ALU(En_ALU), .Select_MUX_Y(Select_MUX_Y),
    .En_MUX_Y(En_MUX_Y), .Load_Write_Ram(Load_Write_Ram), .Enable_to_MUX_Y(Enable_to_MUX_Y), .En_RY(En_RY),
    .Op_Code(Op_Code), .En_Select_RC(En_Select_RC), .En_MUX_B(En_MUX_B), .Select_MUX_B(Select_MUX_B));

  // Other names for the same wires on the sheet: MemoryAddress[18:0] = {CS, Address}; Immediate[31:19] = {13{in_1}}

  // Notes on the sheet:
  //   contents of rom_1 (hex, n*v repeats v):
  //   40080000
endmodule

module Control_Unit (
  input  Load_Signal,
  input  Store_Signal,
  input  Move_Signal,
  input  Jump_Signal,
  input  Signal,
  input  Subtract_Signal,
  input  x_Signal,
  input  Signal_2,
  input  Clock,
  input  [2:0] Op_Code,
  output En_IR,
  output En_PC,
  output Select_MUX_MA,
  output Enable_MUX_MA,
  output Enable_PCSet,
  output Select_PCSet,
  output En_RA,
  output En_RB,
  output En_Select_RA,
  output En_Select_RB,
  output En_RZ,
  output [1:0] Select_ALU,
  output En_RM,
  output En_ALU,
  output Select_MUX_Y,
  output En_MUX_Y,
  output Load_Write_Ram,
  output Enable_to_MUX_Y,
  output En_RY,
  output En_Select_RC,
  output En_MUX_B,
  output Select_MUX_B
);

  wire and_9_out, and_11_out, and_12_out, and_13_out, and_14_out, or_1_out, or_2_out, or_3_out, or_5_out,
       or_6_out, or_8_out, or_10_out, or_11_out, or_13_out, shift_register_1_out, shift_register_1_q3,
       shift_register_1_q4, Stage_1, Stage_2, Stage_3, Stage_4, Stage_5;

  or or_1 (or_1_out, Load_Signal, Store_Signal, Move_Signal, Jump_Signal, Signal, Subtract_Signal, x_Signal, Signal_2);
  or or_2 (or_2_out, Load_Signal, Store_Signal, Move_Signal, Jump_Signal, Signal, Subtract_Signal, x_Signal, Signal_2);
  or or_3 (or_3_out, Load_Signal, Move_Signal, Signal, Subtract_Signal, x_Signal, Signal_2);
  and and_1 (En_IR, Stage_1, or_1_out);
  and and_2 (En_ALU, Stage_3, or_2_out);
  and and_3 (En_MUX_Y, Stage_4, or_3_out);
  or or_4 (Select_MUX_MA, En_IR, Stage_5);
  and and_4 (Enable_to_MUX_Y, Stage_4, Load_Signal);
  or or_5 (or_5_out, Load_Signal, Store_Signal, Move_Signal, Signal, Subtract_Signal, x_Signal, Signal_2);
  and and_5 (En_RM, Stage_3, Store_Signal);
  Shift_Register #(.length(6)) shift_register_1 (
    .shift(1'b1), .in(shift_register_1_out), .clk(Clock), .out(shift_register_1_out), .load(1'b0),
    .q0(Stage_1), .q1(Stage_2), .q2(Stage_3), .q3(shift_register_1_q3), .q4(shift_register_1_q4), .q5(Stage_5));  // open: clr, d0, d1, d2, d3, d4, d5
  and and_6 (Select_PCSet, Stage_1, or_5_out);
  // Probe on Select_ALU
  assign Select_ALU = Op_Code[1:0] & {2{Op_Code[2]}};  // AND_Gate and_7, 2 bits wide
  or or_6 (or_6_out, Load_Signal, Move_Signal, Signal, Subtract_Signal, x_Signal, Signal_2);
  and and_8 (En_Select_RC, Stage_5, or_6_out);
  or or_7 (Stage_4, shift_register_1_q4, shift_register_1_q3);
  and and_9 (and_9_out, Stage_4, Load_Signal);
  or or_8 (or_8_out, Load_Signal, Store_Signal, Move_Signal, Jump_Signal, Signal, Subtract_Signal, x_Signal, Signal_2);
  or or_9 (Enable_MUX_MA, Stage_1, Stage_5, and_9_out);
  and and_10 (En_RA, Stage_2, or_8_out);
  and and_11 (and_11_out, Stage_3, or_10_out);
  or or_10 (or_10_out, Signal, Subtract_Signal, x_Signal, Signal_2);
  and and_12 (and_12_out, Stage_3, or_11_out);
  or or_11 (or_11_out, Load_Signal, Store_Signal, Move_Signal, Jump_Signal, Signal, Subtract_Signal, x_Signal, Signal_2);
  or or_12 (En_RZ, and_11_out, and_12_out);
  or or_13 (or_13_out, Load_Signal, Store_Signal, Move_Signal, Signal, Subtract_Signal, x_Signal, Signal_2);
  and and_13 (and_13_out, Stage_3, Jump_Signal);
  and and_14 (and_14_out, Stage_1, or_13_out);
  or or_14 (Enable_PCSet, and_13_out, and_14_out);

  assign En_MUX_B = 1'b1;
  assign En_PC = En_IR;
  assign En_RB = En_RA;
  assign En_RY = En_MUX_Y;
  assign En_Select_RA = En_RA;
  assign En_Select_RB = En_RA;
  assign Load_Write_Ram = Enable_to_MUX_Y;
  assign Select_MUX_B = 1'b0;
  assign Select_MUX_Y = Enable_to_MUX_Y;

  // Other names for the same wires on the sheet: Signal_t = Signal_2
endmodule
